# Fritzing sketch Home Automation Using Arduino and HC-05 (saved by Fritzing 0.9.3b)
breadboards: 1

parts:
  Part1 = Arduino Uno (Rev3)
  U1 = 2-Channel 5v Relay Shield [package=relay-2ch5v10a]
  Part2 = Bluetooth HC-05 Macho
  LED1 = LED - 5mm [color="Red (633nm)" package="5 mm [THT]"]
  VCC1 = Battery

nets:
  N1: Part1.D0/RX, Part2.TXD
  N2: Part1.D1/TX, Part2.RXD
  N3: Part1.D2, U1.IN1
  N4: Part1.D3_PWM, U1.IN2
  VCC: Part1.5V, U1.VCC, Part2.VCC
  GND: Part1.GND, U1.GND, Part2.GND
  N5: U1.K1-In, LED1.cathode
  N6: U1.K1-On, VCC1.+
  N7: LED1.anode, VCC1.-

custom parts:
  2-Channel 5v Relay Shield: 2 Channel 5v Relay Shield w. 2x SPD-06VDC-SD-C
